# Fritzing sketch sh-simple-focuser (saved by Fritzing 0.9.10b)

parts:
  SM1 = 28BYJ-48 Stepper Motor [part_number=28BYJ-48]
  Driver1 = 28BYJ-48 Driver Module [part_number=ULN2003 package=THT]
  Part1 = Arduino Nano (Rev3.0)
  X1 = USB Connectors [package=usb-mb-h]
  X2 = USB Connectors [package=usb-minib-nostop]

nets:
  N1: SM1.blue-pin, Driver1.blue-pin
  N2: SM1.pink-pin, Driver1.pink-pin
  N3: SM1.yellow-pin, Driver1.yellow-pin
  N4: SM1.orange-pin, Driver1.orange-pin
  N5: SM1.red-pin, Driver1.red-pin
  N6: Driver1.IN1, Part1.D2
  N7: Driver1.IN2, Part1.D3
  N8: Driver1.IN3, Part1.D4
  N9: Driver1.IN4, Part1.D5
  GND: Driver1.GND, X1.GND, X2.GND
  N10: Driver1.Vmotor, X1.VBUS, X2.VBUS
  N11: X1.D+, X2.D+
  N12: X1.D-, X2.D-

notes:
  The USB B connector is used in order to connect the device to the PC using the USB AM/BM cable

custom parts:
  28BYJ-48 Stepper Motor: Unipolar Stepper Motor 28BYJ-48 Top coil - pink & orange Bottom coil - blue & yellow Common rail - red Connector pins: blue - pink - yellow - orange - red
  28BYJ-48 Driver Module: High-power ULN2003 Stepper Motor Driver Board Test Module For Arduino AVR SMD
